// Logisim project 1-bit half adder.circ as structural Verilog: 1 circuit, main circuit main
module main (
  input  x0,
  input  in_2,
  output c,
  output s
);

  and and_1 (c, x0, in_2);
  xor xor_1 (s, x0, in_2);
endmodule
