// Logisim project 2-to-1 multiplexer.circ as structural Verilog: 1 circuit, main circuit main
module main (
  input  x0,
  input  x1,
  input  s,
  output y
);

  wire and_1_out, and_2_out, not_1_out;

  not not_1 (not_1_out, s);
  and and_1 (and_1_out, x0, not_1_out);
  and and_2 (and_2_out, x1, s);
  or or_1 (y, and_1_out, and_2_out);
endmodule
