// Logisim project Gated D latch.circ as structural Verilog: 1 circuit, main circuit main
module main (
  input  D,
  input  E,
  output out_3,
  output out_4
);

  wire nand_1_out, nand_2_out, not_1_out;

  not not_1 (not_1_out, D);
  nand nand_1 (nand_1_out, not_1_out, E);
  nand nand_2 (nand_2_out, E, D);
  nand nand_3 (out_3, nand_1_out, out_4);
  nand nand_4 (out_4, out_3, nand_2_out);
endmodule
